// Logisim project 1bit_4bit_SRAM.circ as structural Verilog: 1 circuit, main circuit main
module main (
  input  A11,
  input  A10,
  input  A9,
  input  A8,
  input  A7,
  input  A6,
  input  A5,
  input  A4,
  input  A3,
  input  A2,
  input  A1,
  input  A0,
  input  DIP0,
  input  DIP1,
  input  WRT,
  input  DIN
);

  wire and_2_out, and_3_out, clock_1_out, demultiplexer_1_out0, demultiplexer_1_out1, demultiplexer_1_out2,
       demultiplexer_1_out3, demultiplexer_2_out4, demultiplexer_2_out5, demultiplexer_2_out6,
       demultiplexer_2_out7, multiplexer_1_out, nor_1_out, not_1_out, or_1_out, pull_resistor_1_node,
       pull_resistor_2_node;
  wire [2:2] and_1_out;
  wire [3:0] multiplexer_2_out, ram_1_dout;

  LED DOUT (.in(and_3_out));
  Pull_Resistor #(.pull(1)) pull_resistor_1 (.node(pull_resistor_1_node));
  Demultiplexer #(.enable("false"), .select(2)) demultiplexer_1 (
    .out0(demultiplexer_1_out0), .out1(demultiplexer_1_out1), .out2(demultiplexer_1_out2),
    .out3(demultiplexer_1_out3), .in(pull_resistor_1_node), .sel({A11, A10}));
  Multiplexer #(.enable("false"), .select(2)) multiplexer_1 (
    .in0(demultiplexer_1_out0), .in1(demultiplexer_1_out1), .in2(demultiplexer_1_out2),
    .in3(demultiplexer_1_out3), .out(multiplexer_1_out), .sel({DIP1, DIP0}));
  and and_1 (and_1_out[2], WRT, multiplexer_1_out);
  and and_2 (and_2_out, DIN, multiplexer_1_out);
  and and_3 (and_3_out, multiplexer_1_out, nor_1_out);
  Pull_Resistor #(.pull(1)) pull_resistor_2 (.node(pull_resistor_2_node));
  Demultiplexer #(.enable("false"), .select(3)) demultiplexer_2 (
    .out4(demultiplexer_2_out4), .out5(demultiplexer_2_out5), .out6(demultiplexer_2_out6),
    .out7(demultiplexer_2_out7), .in(pull_resistor_2_node), .sel({and_1_out[2], A9, A8}));  // open: out0, out1, out2, out3
  Multiplexer #(.enable("false")) multiplexer_2 (
    .in0(ram_1_dout[0]), .in1(and_2_out), .out(multiplexer_2_out[0]), .sel(demultiplexer_2_out4));
  Multiplexer #(.enable("false")) multiplexer_3 (
    .in0(ram_1_dout[1]), .in1(and_2_out), .out(multiplexer_2_out[1]), .sel(demultiplexer_2_out5));
  Multiplexer #(.enable("false")) multiplexer_4 (
    .in0(ram_1_dout[2]), .in1(and_2_out), .out(multiplexer_2_out[2]), .sel(demultiplexer_2_out6));
  Multiplexer #(.enable("false")) multiplexer_5 (
    .in0(ram_1_dout[3]), .in1(and_2_out), .out(multiplexer_2_out[3]), .sel(demultiplexer_2_out7));
  RAM #(.dataWidth(4), .enables("line")) ram_1 (
    .addr({A7, A6, A5, A4, A3, A2, A1, A0}), .we(and_1_out[2]), .clk(clock_1_out), .din(multiplexer_2_out),
    .dout(ram_1_dout));
  Clock clock_1 (.out(clock_1_out));
  or or_1 (or_1_out, multiplexer_2_out[0], multiplexer_2_out[1], multiplexer_2_out[2], multiplexer_2_out[3]);
  not not_1 (not_1_out, or_1_out);
  nor nor_1 (nor_1_out, not_1_out, and_1_out[2]);

  // Notes on the sheet:
  //   A0~A7 = Address
  //   WRT = Write
  //   A8~A9 = Bank Select
endmodule
