// Logisim project HaltResume.circ as structural Verilog: 1 circuit, main circuit main
module main (
  output out_1
);

  wire clock_1_out, nand_1_out, nand_2_out, nand_3_out, nand_4_out, nand_5_out, nand_6_out, nand_7_out,
       nand_8_out, nand_10_out;

  Clock clock_1 (.out(clock_1_out));
  nand nand_1 (nand_1_out, out_1, out_1);
  nand nand_2 (nand_2_out, nand_1_out, clock_1_out);
  nand nand_3 (nand_3_out, nand_2_out, clock_1_out);
  nand nand_4 (nand_4_out, nand_2_out, nand_5_out);
  nand nand_5 (nand_5_out, nand_4_out, nand_3_out);
  nand nand_6 (nand_6_out, clock_1_out, clock_1_out);
  nand nand_7 (nand_7_out, nand_4_out, nand_6_out);
  nand nand_8 (nand_8_out, nand_7_out, nand_6_out);
  nand nand_9 (out_1, nand_7_out, nand_10_out);
  nand nand_10 (nand_10_out, out_1, nand_8_out);
endmodule
