// Logisim project HexDisplayROM.circ as structural Verilog: 1 circuit, main circuit main
module main (
  input  RST,
  input  PC_CLK
);

  wire and_1_out, and_2_out, and_3_out, and_4_out, and_5_out, and_6_out, and_7_out, and_8_out, and_9_out,
       and_10_out, and_11_out, and_12_out, decoder_1_out0, decoder_1_out1, decoder_1_out2, decoder_1_out3,
       DISP_CLK_out, not_1_out;
  wire [1:0] counter_1_q;
  wire [3:0] or_1_out;
  wire [7:0] rom_1_data;
  wire [11:0] counter_2_q;

  Clock DISP_CLK (.out(DISP_CLK_out));
  Counter #(.max('h3), .width(2)) counter_1 (
    .clk(DISP_CLK_out), .Q(counter_1_q));  // open: clr, load, up, count, D, carry
  Counter #(.max('hfff), .width(12)) counter_2 (
    .clr(RST), .clk(PC_CLK), .Q(counter_2_q));  // open: load, up, count, D, carry
  Decoder #(.select(2)) decoder_1 (
    .out0(decoder_1_out0), .out1(decoder_1_out1), .out2(decoder_1_out2), .out3(decoder_1_out3),
    .sel(counter_1_q));  // open: en
  not not_1 (not_1_out, decoder_1_out3);
  and and_1 (and_1_out, decoder_1_out2, counter_2_q[0]);
  and and_2 (and_2_out, decoder_1_out2, counter_2_q[1]);
  and and_3 (and_3_out, decoder_1_out2, counter_2_q[2]);
  and and_4 (and_4_out, decoder_1_out2, counter_2_q[3]);
  and and_5 (and_5_out, decoder_1_out1, counter_2_q[4]);
  and and_6 (and_6_out, decoder_1_out1, counter_2_q[5]);
  and and_7 (and_7_out, decoder_1_out1, counter_2_q[6]);
  and and_8 (and_8_out, decoder_1_out1, counter_2_q[7]);
  and and_9 (and_9_out, decoder_1_out0, counter_2_q[8]);
  and and_10 (and_10_out, decoder_1_out0, counter_2_q[9]);
  and and_11 (and_11_out, decoder_1_out0, counter_2_q[10]);
  and and_12 (and_12_out, decoder_1_out0, counter_2_q[11]);
  LED GRID_BLANK (.in(not_1_out));
  or or_1 (or_1_out[0], and_1_out, and_5_out, and_9_out);
  or or_2 (or_1_out[1], and_2_out, and_6_out, and_10_out);
  or or_3 (or_1_out[2], and_3_out, and_7_out, and_11_out);
  or or_4 (or_1_out[3], and_4_out, and_8_out, and_12_out);
  ROM #(.addrWidth(4)) rom_1 (.addr(or_1_out), .data(rom_1_data));
  _7_Segment_Display u_7_segment_display_1 (
    .g(rom_1_data[6]), .f(rom_1_data[5]), .a(rom_1_data[0]), .b(rom_1_data[1]), .e(rom_1_data[4]),
    .d(rom_1_data[3]), .c(rom_1_data[2]), .dp(decoder_1_out3));

  // Notes on the sheet:
  //   contents of rom_1 (hex, n*v repeats v):
  //   3f 6 5b 4f 66 6d 7d 7 7f 6f 77 7c 39 5e 79 71
endmodule
