// Logisim project HexDisplayROM_v2.circ as structural Verilog: 1 circuit, main circuit main
module main (
  input  RST,
  input  PC_CLK
);

  wire decoder_1_out3, DISP_CLK_out, not_1_out;
  wire [1:0] counter_1_q;
  wire [7:0] rom_1_data;
  wire [11:0] counter_2_q;
  wire [14:12] decoder_1_out0;

  Clock DISP_CLK (.out(DISP_CLK_out));
  Counter #(.max('h3), .width(2)) counter_1 (
    .clk(DISP_CLK_out), .Q(counter_1_q));  // open: clr, load, up, count, D, carry
  Counter #(.max('hfff), .width(12)) counter_2 (
    .clr(RST), .clk(PC_CLK), .Q(counter_2_q));  // open: load, up, count, D, carry
  Decoder #(.select(2)) decoder_1 (
    .out0(decoder_1_out0[12]), .out1(decoder_1_out0[13]), .out2(decoder_1_out0[14]), .out3(decoder_1_out3),
    .sel(counter_1_q));  // open: en
  not not_1 (not_1_out, decoder_1_out3);
  ROM #(.addrWidth(15)) rom_1 (.addr({decoder_1_out0, counter_2_q}), .data(rom_1_data));
  LED GRID_BLANK (.in(not_1_out));
  _7_Segment_Display u_7_segment_display_1 (
    .g(rom_1_data[6]), .f(rom_1_data[5]), .a(rom_1_data[0]), .b(rom_1_data[1]), .e(rom_1_data[4]),
    .d(rom_1_data[3]), .c(rom_1_data[2]), .dp(decoder_1_out3));

  // Notes on the sheet:
  //   contents of rom_1 (hex, n*v repeats v):
  //   3f 6 5b 4f 66 6d 7d 7 7f 6f 77 7c 39 5e 79 71
endmodule
