// Logisim project MMIO.circ as structural Verilog: 1 circuit, main circuit main
module main (
  input  in_1,
  input  in_2,
  input  in_3,
  input  in_4,
  input  in_5,
  input  in_6,
  input  in_7,
  input  in_8,
  input  in_9,
  input  in_10,
  input  in_11,
  input  in_12,
  input  RR,
  input  QRR,
  input  CAR,
  input  QCAR,
  output DATA,
  output FF4,
  output Q_FFX
);

  wire multiplexer_1_out, nand_1_out, nand_2_out, nand_3_out, not_2_out, not_3_out, not_4_out, not_5_out;

  nand nand_1 (nand_1_out, in_1, in_2, in_3, in_4, in_5, in_6, in_7, in_8);
  not not_1 (Q_FFX, nand_1_out);
  not not_2 (not_2_out, in_9);
  not not_3 (not_3_out, in_10);
  nand nand_2 (nand_2_out, not_3_out, not_2_out, Q_FFX);
  nand nand_3 (nand_3_out, not_2_out, in_10, Q_FFX);
  Multiplexer #(.select(2), .disabled(0)) multiplexer_1 (
    .in0(QCAR), .in1(CAR), .in2(QRR), .in3(RR), .out(multiplexer_1_out), .sel({in_11, in_12}), .en(not_4_out));
  not not_4 (not_4_out, nand_2_out);
  Multiplexer #(.select(2), .disabled(0)) multiplexer_2 (
    .in0(1'b1), .in1(1'b0), .in2(1'b0), .in3(1'b0), .out(FF4), .sel({in_11, in_12}), .en(not_5_out));
  not not_5 (not_5_out, nand_3_out);
  or or_1 (DATA, multiplexer_1_out, FF4);
endmodule
