// Logisim project RTN.circ as structural Verilog: 1 circuit, main circuit main
module main (
  input  JMP,
  input  RTN
);

  wire clock_1_out;
  wire [3:0] adder_1_out_2, multiplexer_1_out_2;
  wire [7:0] adder_1_out, multiplexer_1_out;
  wire [11:0] counter_1_q, RA_q;

  Counter #(.max('hfff), .width(12)) counter_1 (
    .clk(clock_1_out), .Q(counter_1_q));  // open: clr, load, up, count, D, carry
  Clock clock_1 (.out(clock_1_out));
  Register #(.width(12)) RA (.D(counter_1_q), .clk(JMP), .Q(RA_q));  // open: en, clr
  Multiplexer #(.enable("false"), .width(12)) multiplexer_1 (
    .in0(counter_1_q), .in1({adder_1_out_2, adder_1_out}), .out({multiplexer_1_out_2, multiplexer_1_out}),
    .sel(RTN));
  Adder #(.width(12)) adder_1 (.a(RA_q), .b(12'h1), .out({adder_1_out_2, adder_1_out}), .cin(1'b0));  // open: cout
  Hex_Digit_Display hex_digit_display_1 (.value(multiplexer_1_out_2));  // open: dp
  Hex_Digit_Display hex_digit_display_2 (.value(adder_1_out_2));  // open: dp
  Hex_Digit_Display hex_digit_display_3 (.value(adder_1_out[7:4]));  // open: dp
  Hex_Digit_Display hex_digit_display_4 (.value(multiplexer_1_out[7:4]));  // open: dp
  Hex_Digit_Display hex_digit_display_5 (.value(multiplexer_1_out[3:0]));  // open: dp
  Hex_Digit_Display hex_digit_display_6 (.value(adder_1_out[3:0]));  // open: dp
endmodule
