// Logisim project Scratch.circ as structural Verilog: 1 circuit, main circuit main
module main (
  input  D0,
  input  AD0,
  input  D1,
  input  AD1,
  input  D2,
  input  AD2,
  input  D3,
  input  AD3,
  input  DBUS,
  input  WRT,
  input  P_READ,
  input  P_COPY,
  output TO_MEM,
  output TO_MEM_2,
  output TO_MEM_3,
  output TO_MEM_4,
  output TO_DBUS
);

  wire and_1_out, and_2_out, and_4_out, and_5_out, and_6_out, and_7_out, and_8_out, and_10_out, and_11_out,
       and_13_out, and_14_out, and_15_out, d_ff_1_q, d_ff_2_q, d_ff_3_q, d_ff_4_q, not_1_out, not_2_out,
       not_3_out, not_4_out, or_1_out, or_2_out, or_3_out, or_4_out, or_5_out, or_6_out, or_8_out, or_9_out;

  and and_1 (and_1_out, D0, P_READ);
  or or_1 (or_1_out, DBUS, and_1_out);
  and and_2 (and_2_out, WRT, AD0);
  or or_2 (or_2_out, P_READ, and_2_out);
  D_Flip_Flop #(.trigger("high")) d_ff_1 (.clk(or_2_out), .D(or_1_out), .Q(d_ff_1_q));  // open: Qn, preset, en, reset
  not not_1 (not_1_out, WRT);
  and and_3 (TO_MEM, d_ff_1_q, P_COPY);
  and and_4 (and_4_out, not_1_out, AD0, d_ff_1_q);
  and and_5 (and_5_out, WRT, AD1);
  and and_6 (and_6_out, D1, P_READ);
  or or_3 (or_3_out, DBUS, and_6_out);
  or or_4 (or_4_out, P_READ, and_5_out);
  D_Flip_Flop #(.trigger("high")) d_ff_2 (.clk(or_4_out), .D(or_3_out), .Q(d_ff_2_q));  // open: Qn, preset, en, reset
  not not_2 (not_2_out, WRT);
  and and_7 (and_7_out, not_2_out, AD1, d_ff_2_q);
  and and_8 (and_8_out, D2, P_READ);
  or or_5 (or_5_out, DBUS, and_8_out);
  and and_9 (TO_MEM_2, d_ff_2_q, P_COPY);
  and and_10 (and_10_out, WRT, AD2);
  or or_6 (or_6_out, P_READ, and_10_out);
  D_Flip_Flop #(.trigger("high")) d_ff_3 (.clk(or_6_out), .D(or_5_out), .Q(d_ff_3_q));  // open: Qn, preset, en, reset
  or or_7 (TO_DBUS, and_4_out, and_7_out, and_11_out, and_15_out);
  not not_3 (not_3_out, WRT);
  and and_11 (and_11_out, not_3_out, AD2, d_ff_3_q);
  and and_12 (TO_MEM_3, d_ff_3_q, P_COPY);
  and and_13 (and_13_out, D3, P_READ);
  and and_14 (and_14_out, WRT, AD3);
  or or_8 (or_8_out, DBUS, and_13_out);
  or or_9 (or_9_out, P_READ, and_14_out);
  D_Flip_Flop #(.trigger("high")) d_ff_4 (.clk(or_9_out), .D(or_8_out), .Q(d_ff_4_q));  // open: Qn, preset, en, reset
  not not_4 (not_4_out, WRT);
  and and_15 (and_15_out, not_4_out, AD3, d_ff_4_q);
  and and_16 (TO_MEM_4, d_ff_4_q, P_COPY);
endmodule
