// Logisim project SimplifiedROM.circ as structural Verilog: 1 circuit, main circuit main
module main (
  input  in_1,
  output SYS_CLK
);

  wire clock_1_out;
  wire [2:0] register_2_q;
  wire [3:0] register_1_q;
  wire [7:0] counter_1_q, rom_1_data;

  Clock clock_1 (.out(clock_1_out));
  Counter counter_1 (.Q(counter_1_q), .clk(clock_1_out), .clr(in_1));  // open: load, D, count, carry
  ROM rom_1 (.addr(counter_1_q), .data(rom_1_data));  // open: sel
  Register #(.width(4)) register_1 (
    .D(rom_1_data[3:0]), .Q(register_1_q), .clk(rom_1_data[7]), .clr(in_1));  // open: en
  Register #(.width(3)) register_2 (
    .D(rom_1_data[6:4]), .Q(register_2_q), .clk(rom_1_data[7]), .clr(in_1));  // open: en
  not not_1 (SYS_CLK, rom_1_data[7]);

  // Notes on the sheet:
  //   contents of rom_1 (hex, n*v repeats v):
  //   0 95 77 94
endmodule
