// Logisim project StateMachine.circ as structural Verilog: 1 circuit, main circuit main
module main (
  input  RESET
);

  wire and_1_out, and_2_out, and_3_out, and_4_out, clock_1_out, demultiplexer_1_out1, demultiplexer_1_out2,
       demultiplexer_1_out3, demultiplexer_1_out4, demultiplexer_1_out5, demultiplexer_1_out7, nand_1_out,
       nand_2_out, nand_3_out, not_1_out, not_2_out, not_3_out, or_1_out, or_2_out;
  wire [2:0] counter_2_q;
  wire [3:0] register_3_q, register_3_q_2;
  wire [7:0] controlled_buffer_1_out, register_1_q, register_2_q, rom_1_data;
  wire [15:0] counter_1_q, counter_3_q;

  Clock clock_1 (.out(clock_1_out));
  not not_1 (not_1_out, nand_1_out);
  Counter #(.width(16), .max('hffff)) counter_1 (
    .Q(counter_1_q), .clk(and_1_out), .clr(or_2_out));  // open: load, D, count, carry
  and and_1 (and_1_out, nand_1_out, clock_1_out);
  and and_2 (and_2_out, not_1_out, clock_1_out);
  nand nand_1 (nand_1_out, counter_1_q[0], counter_1_q[1], counter_1_q[2], counter_1_q[3], counter_1_q[4], counter_1_q[5], counter_1_q[6], counter_1_q[7], counter_1_q[9], counter_1_q[10], counter_1_q[11], counter_1_q[12], counter_1_q[13], counter_1_q[14], counter_1_q[15], counter_1_q[8]);
  and and_3 (and_3_out, nand_1_out, clock_1_out);
  Demultiplexer #(.select(3)) demultiplexer_1 (
    .out1(demultiplexer_1_out1), .out2(demultiplexer_1_out2), .out3(demultiplexer_1_out3),
    .out4(demultiplexer_1_out4), .out5(demultiplexer_1_out5), .out6(demultiplexer_1_out5),
    .out7(demultiplexer_1_out7), .in(1'b1), .sel(counter_2_q));  // open: out0, en
  Counter #(.width(3), .max('h7)) counter_2 (
    .Q(counter_2_q), .clk(and_2_out), .clr(or_2_out));  // open: load, D, count, carry
  assign controlled_buffer_1_out = nand_1_out ? rom_1_data : 8'bz;  // Controlled_Buffer controlled_buffer_1
  ROM #(.addrWidth(16)) rom_1 (.addr(counter_1_q), .data(rom_1_data));  // open: sel
  or or_1 (or_1_out, and_3_out, demultiplexer_1_out2, demultiplexer_1_out5, demultiplexer_1_out7);
  or or_2 (or_2_out, and_4_out, RESET);
  Counter #(.width(16), .max('hffff)) counter_3 (
    .Q(counter_3_q), .clk(or_1_out), .clr(or_2_out));  // open: load, D, count, carry
  and and_4 (and_4_out, demultiplexer_1_out3, nand_2_out, nand_3_out);
  nand nand_2 (nand_2_out, register_2_q[4], register_2_q[5], register_2_q[6], register_2_q[7]);
  nand nand_3 (nand_3_out, register_2_q[5], register_2_q[4], not_2_out, not_3_out);
  not not_2 (not_2_out, register_2_q[6]);
  not not_3 (not_3_out, register_2_q[7]);
  RAM #(.addrWidth(16)) ram_1 (
    .addr(counter_3_q), .data(controlled_buffer_1_out), .clk(and_1_out), .ld(and_1_out));  // open: sel, clr
  Register register_1 (.D(controlled_buffer_1_out), .Q(register_1_q), .clk(demultiplexer_1_out4));  // open: en, clr
  Register register_2 (.D(controlled_buffer_1_out), .Q(register_2_q), .clk(demultiplexer_1_out1));  // open: en, clr
  Hex_Digit_Display hex_digit_display_1 (.value(register_2_q[7:4]));  // open: dp
  Register register_3 (
    .D(controlled_buffer_1_out), .Q({register_3_q_2, register_3_q}), .clk(demultiplexer_1_out5));  // open: en, clr
  Hex_Digit_Display hex_digit_display_2 (.value(register_2_q[3:0]));  // open: dp
  Hex_Digit_Display hex_digit_display_3 (.value(register_1_q[7:4]));  // open: dp
  Hex_Digit_Display hex_digit_display_4 (.value(register_1_q[3:0]));  // open: dp
  Hex_Digit_Display hex_digit_display_5 (.value(register_3_q));  // open: dp
  Hex_Digit_Display hex_digit_display_6 (.value(register_3_q_2));  // open: dp

  // Notes on the sheet:
  //   contents of rom_1 (hex, n*v repeats v):
  //   12 34 56 78 9a bc de f1 ed cb a9 87 65 43 21
endmodule
