// Logisim project StateMachine_Evol.circ as structural Verilog: 1 circuit, main circuit main
module main (
  input  SCW,
  input  RST
);

  wire and_1_out, and_2_out, and_3_out, and_4_out, clock_1_out, demultiplexer_1_out1, demultiplexer_1_out2,
       demultiplexer_1_out3, demultiplexer_1_out4, demultiplexer_1_out5, demultiplexer_1_out6,
       demultiplexer_1_out7, nand_1_out, nand_2_out, nand_3_out, not_1_out, not_2_out, not_3_out, not_4_out,
       not_5_out, not_6_out, not_7_out, not_8_out, not_9_out, not_10_out, or_1_out, or_2_out, or_3_out;
  wire [2:0] counter_1_q;
  wire [3:0] register_1_q;
  wire [7:0] controlled_buffer_1_out, ram_1_dout, register_2_q, register_3_q, rom_1_data;
  wire [7:4] register_1_q_2;
  wire [15:0] counter_2_q, counter_3_q;

  Clock clock_1 (.out(clock_1_out));
  not not_1 (not_1_out, nand_1_out);
  and and_1 (and_1_out, nand_1_out, clock_1_out);
  and and_2 (and_2_out, not_1_out, clock_1_out);
  Demultiplexer #(.enable("false"), .select(3)) demultiplexer_1 (
    .out1(demultiplexer_1_out1), .out2(demultiplexer_1_out2), .out3(demultiplexer_1_out3),
    .out4(demultiplexer_1_out4), .out5(demultiplexer_1_out5), .out6(demultiplexer_1_out6),
    .out7(demultiplexer_1_out7), .in(1'b1), .sel(counter_1_q));  // open: out0
  Counter #(.max('h7), .width(3)) counter_1 (
    .Q(counter_1_q), .clk(and_2_out), .clr(or_2_out));  // open: load, D, count, carry, up
  nand nand_1 (nand_1_out, counter_2_q[0], counter_2_q[1], counter_2_q[2], counter_2_q[3], counter_2_q[4], counter_2_q[5], counter_2_q[6], counter_2_q[7], counter_2_q[9], counter_2_q[10], counter_2_q[11], counter_2_q[12], counter_2_q[13], counter_2_q[14], counter_2_q[15], counter_2_q[8]);
  and and_3 (and_3_out, nand_1_out, clock_1_out);
  Counter #(.max('hffff), .width(16)) counter_2 (
    .Q(counter_2_q), .clk(and_1_out), .clr(or_2_out));  // open: load, D, count, carry, up
  or or_1 (or_1_out, and_3_out, demultiplexer_1_out2, demultiplexer_1_out5, demultiplexer_1_out7);
  or or_2 (or_2_out, and_4_out, RST);
  not not_2 (not_2_out, and_1_out);
  not not_3 (not_3_out, not_5_out);
  Counter #(.max('hffff), .width(16)) counter_3 (
    .Q(counter_3_q), .clk(or_1_out), .clr(or_2_out));  // open: load, D, count, carry, up
  nand nand_2 (nand_2_out, register_1_q_2[4], register_1_q_2[5], register_1_q_2[6], register_1_q_2[7]);
  and and_4 (and_4_out, demultiplexer_1_out3, nand_2_out, nand_3_out);
  nand nand_3 (nand_3_out, register_1_q_2[4], register_1_q_2[5], not_8_out, not_9_out);
  not not_4 (not_4_out, not_2_out);
  not not_5 (not_5_out, not_4_out);
  not not_6 (not_6_out, not_3_out);
  not not_7 (not_7_out, not_6_out);
  or or_3 (or_3_out, not_7_out, SCW);
  not not_8 (not_8_out, register_1_q_2[7]);
  not not_9 (not_9_out, register_1_q_2[6]);
  ROM #(.addrWidth(16)) rom_1 (.addr(counter_2_q), .data(rom_1_data));
  RAM #(.addrWidth(16)) ram_1 (
    .addr(counter_3_q), .we(or_3_out), .oe(not_10_out), .clk(or_3_out), .din(controlled_buffer_1_out),
    .dout(ram_1_dout));
  not not_10 (not_10_out, or_3_out);
  Register register_1 (
    .D(ram_1_dout), .Q({register_1_q_2, register_1_q}), .clk(demultiplexer_1_out1), .clr(or_2_out));  // open: en
  Register register_2 (.D(ram_1_dout), .Q(register_2_q), .clk(demultiplexer_1_out4), .clr(or_2_out));  // open: en
  assign controlled_buffer_1_out = nand_1_out ? rom_1_data : 8'bz;  // Controlled_Buffer controlled_buffer_1
  Register register_3 (.D(ram_1_dout), .Q(register_3_q), .clk(demultiplexer_1_out6), .clr(or_2_out));  // open: en

  // Notes on the sheet:
  //   contents of rom_1 (hex, n*v repeats v):
  //   0 1 2 3 4 5 6 7 8 9 a b c d e f 10 11 12 13 14 15 16 17 18 19 1a 1b 1c 1d 1e 1f
endmodule
