// Logisim project StateMachine_v2_Evol.circ as structural Verilog: 1 circuit, main circuit main
module main (
  input  SCW,
  input  RST
);

  wire and_1_out, clock_1_out, demultiplexer_1_out1, demultiplexer_1_out2, demultiplexer_1_out3,
       demultiplexer_1_out4, demultiplexer_1_out5, demultiplexer_1_out6, demultiplexer_1_out7, nand_1_out,
       nand_2_out, not_1_out, not_2_out, not_3_out, not_4_out, not_5_out, or_1_out, or_2_out, or_3_out,
       or_4_out, undriven;
  wire [2:0] counter_1_q;
  wire [3:0] register_1_q;
  wire [7:0] controlled_buffer_1_out, ram_1_dout, register_2_q, register_3_q, rom_1_data;
  wire [7:4] register_1_q_2;
  wire [11:0] counter_2_q;

  Demultiplexer #(.enable("false"), .select(3)) demultiplexer_1 (
    .out1(demultiplexer_1_out1), .out2(demultiplexer_1_out2), .out3(demultiplexer_1_out3),
    .out4(demultiplexer_1_out4), .out5(demultiplexer_1_out5), .out6(demultiplexer_1_out6),
    .out7(demultiplexer_1_out7), .in(1'b1), .sel(counter_1_q));  // open: out0
  Counter #(.max('h7), .width(3)) counter_1 (
    .Q(counter_1_q), .clk(clock_1_out), .clr(or_1_out));  // open: load, D, count, carry, up
  Clock clock_1 (.out(clock_1_out));
  or or_1 (or_1_out, and_1_out, RST);
  Counter #(.max('hfff), .width(12)) counter_2 (
    .Q(counter_2_q), .clk(or_2_out), .clr(RST));  // open: load, D, count, carry, up
  or or_2 (or_2_out, demultiplexer_1_out2, demultiplexer_1_out5, demultiplexer_1_out7);
  D_Flip_Flop d_ff_1 (.clk(demultiplexer_1_out1), .reset(RST));  // open: D, Q, Qn, preset
  not not_1 (not_1_out, undriven);
  nand nand_1 (nand_1_out, register_1_q_2[4], register_1_q_2[5], register_1_q_2[6], register_1_q_2[7]);
  and and_1 (and_1_out, demultiplexer_1_out3, nand_1_out, nand_2_out);
  nand nand_2 (nand_2_out, register_1_q_2[4], register_1_q_2[5], not_2_out, not_3_out);
  or or_3 (or_3_out, not_1_out, SCW);
  or or_4 (or_4_out, or_3_out, RST);
  not not_2 (not_2_out, register_1_q_2[7]);
  not not_3 (not_3_out, register_1_q_2[6]);
  ROM #(.addrWidth(12)) rom_1 (.addr(counter_2_q), .data(rom_1_data));
  RAM #(.addrWidth(12)) ram_1 (
    .addr(counter_2_q), .we(or_3_out), .oe(not_4_out), .clk(demultiplexer_1_out1),
    .din(controlled_buffer_1_out), .dout(ram_1_dout));
  not not_4 (not_4_out, or_3_out);
  Register register_1 (
    .D(controlled_buffer_1_out), .Q({register_1_q_2, register_1_q}), .clk(demultiplexer_1_out1),
    .clr(or_4_out));  // open: en
  Register register_2 (
    .D(controlled_buffer_1_out), .Q(register_2_q), .clk(demultiplexer_1_out4), .clr(or_4_out));  // open: en
  assign controlled_buffer_1_out = not_5_out ? rom_1_data : 8'bz;  // Controlled_Buffer controlled_buffer_1
  not not_5 (not_5_out, undriven);
  assign controlled_buffer_1_out = undriven ? ram_1_dout : 8'bz;  // Controlled_Buffer controlled_buffer_2
  Register register_3 (
    .D(controlled_buffer_1_out), .Q(register_3_q), .clk(demultiplexer_1_out6), .clr(or_4_out));  // open: en

  // Notes on the sheet:
  //   contents of rom_1 (hex, n*v repeats v):
  //   0 1 2 3 4 5 6 7 8 9 a b c d e f 10 11 12 13 14 15 16 17 18 19 1a 1b 1c 1d 1e 1f
endmodule
