// Logisim project StateMachine_v3_Evol.circ as structural Verilog: 1 circuit, main circuit main
module main (
  input  RST
);

  wire clock_1_out, demultiplexer_1_out1, demultiplexer_1_out2, demultiplexer_1_out3, demultiplexer_1_out5,
       demultiplexer_1_out7, not_1_out, or_1_out, or_2_out, undriven, undriven_2, undriven_3, undriven_4;
  wire [2:0] counter_1_q;
  wire [7:0] controlled_buffer_1_out, ram_1_dout, register_1_q, register_2_q, rom_1_data;
  wire [11:0] counter_2_q;

  Demultiplexer #(.enable("false"), .select(3)) demultiplexer_1 (
    .out1(demultiplexer_1_out1), .out2(demultiplexer_1_out2), .out3(demultiplexer_1_out3),
    .out5(demultiplexer_1_out5), .out7(demultiplexer_1_out7), .in(1'b1), .sel(counter_1_q));  // open: out0, out4, out6
  Counter #(.max('h7), .width(3)) counter_1 (
    .Q(counter_1_q), .clk(clock_1_out), .clr(or_1_out));  // open: load, D, count, carry, up
  Clock clock_1 (.out(clock_1_out));
  buf or_1 (or_1_out, RST);  // OR_Gate
  Counter #(.max('hfff), .width(12)) counter_2 (
    .Q(counter_2_q), .clk(or_2_out), .clr(RST));  // open: load, D, count, carry, up
  or or_2 (or_2_out, demultiplexer_1_out2, demultiplexer_1_out5, demultiplexer_1_out7);
  ROM #(.addrWidth(11)) rom_1 (.addr(counter_2_q[10:0]), .data(rom_1_data));
  RAM #(.addrWidth(11)) ram_1 (
    .addr(counter_2_q[10:0]), .din(controlled_buffer_1_out), .dout(ram_1_dout));  // open: we, oe, clk
  Register register_1 (
    .D(controlled_buffer_1_out), .en(undriven), .Q(register_1_q), .clk(undriven_3), .clr(undriven_4));
  assign controlled_buffer_1_out = not_1_out ? rom_1_data : 8'bz;  // Controlled_Buffer controlled_buffer_1
  not not_1 (not_1_out, counter_2_q[11]);
  assign controlled_buffer_1_out = counter_2_q[11] ? ram_1_dout : 8'bz;  // Controlled_Buffer controlled_buffer_2
  Register register_2 (
    .D(controlled_buffer_1_out), .en(undriven_2), .Q(register_2_q), .clk(undriven_3), .clr(undriven_4));

  // Notes on the sheet:
  //   contents of rom_1 (hex, n*v repeats v):
  //   0 1 2 3 4 5 6 7 8 9 a b c d e f 10 11 12 13 14 15 16 17 18 19 1a 1b 1c 1d 1e 1f
endmodule
