// Logisim project UEROM.circ as structural Verilog: 1 circuit, main circuit main
module main (
  input  DATA,
  input  I3,
  input  I2,
  input  I1,
  input  I0
);

  wire and_1_out, and_3_out, and_4_out, and_5_out, and_6_out, and_7_out, CLK_out, IEN_q, not_1_out,
       not_2_out, not_3_out, not_4_out, not_5_out, OEN_q, or_1_out;
  wire [3:1] CAR_q;
  wire [7:0] register_1_q, rom_1_data;

  Clock CLK (.out(CLK_out));
  not not_1 (not_1_out, I2);
  not not_2 (not_2_out, I0);
  and and_1 (and_1_out, I3, I1, not_1_out, not_2_out, CLK_out);
  D_Flip_Flop IEN (.D(or_1_out), .clk(and_1_out), .Q(IEN_q));  // open: Qn, preset, reset
  and and_2 (CAR_q[3], IEN_q, or_1_out);
  Register register_1 (.D({I3, I2, I1, I0, CAR_q, 1'b0}), .clk(CLK_out), .Q(register_1_q));  // open: en, clr
  not not_3 (not_3_out, CLK_out);
  or or_1 (or_1_out, DATA, and_3_out, and_4_out);
  and and_3 (and_3_out, I0, rom_1_data[7], not_4_out);
  and and_4 (and_4_out, not_5_out, rom_1_data[7], CAR_q[2]);
  not not_4 (not_4_out, CAR_q[2]);
  not not_5 (not_5_out, I0);
  ROM rom_1 (.addr(register_1_q), .data(rom_1_data));
  D_Flip_Flop OEN (.D(or_1_out), .clk(and_5_out), .Q(OEN_q));  // open: Qn, preset, reset
  and and_5 (and_5_out, not_1_out, I0, I1, I3, CLK_out);
  D_Flip_Flop CAR (.D(rom_1_data[1]), .clk(not_3_out), .Q(CAR_q[1]));  // open: Qn, preset, reset
  D_Flip_Flop RR (.D(rom_1_data[0]), .clk(not_3_out), .Q(CAR_q[2]));  // open: Qn, preset, reset
  and and_6 (and_6_out, OEN_q, CLK_out, rom_1_data[6]);
  LED WRT (.in(and_6_out));
  LED RR_OUT (.in(CAR_q[2]));
  LED FLG0 (.in(rom_1_data[2]));
  and and_7 (and_7_out, CAR_q[2], rom_1_data[3]);
  LED JMP (.in(and_7_out));
  LED RTN (.in(rom_1_data[4]));
  LED FLGF (.in(rom_1_data[5]));

  // Notes on the sheet:
  //   contents of rom_1 (hex, n*v repeats v):
  //   4 0 6 0 5 0 7 0 4 0 6 0 5 0 7 0 0 0 2 0 0 0 2 0 1 0 3 0 1 0 3 0 0 0 1 0 1 0 2 0 1 0 2 0 2 0 3 0 1 0
  //   2 0 2 0 3 0 0 0 1 0 1 0 2 0 1 0 1 0 1 0 1 0 1 0 1 0 1 0 1 0 1 0 3 0 1 0 3 0 1 0 3 0 0 0 2 0 0 0 2 0
  //   1 0 3 0 1 0 3 0 1 0 3 0 0 0 2 0 1 0 3 0 1 0 3 0 0 0 2 0 c0 0 c2 0 c1 0 c3 0 c0 0 c2 0 c1 0 c3 0 c0 0
  //   c2 0 c1 0 c3 0 c0 0 c2 0 c1 0 c3 0 0 0 2 0 1 0 3 0 0 0 2 0 1 0 3 0 0 0 2 0 1 0 3 0 0 0 2 0 1 0 3 0 8
  //   0 a 0 9 0 b 0 8 0 a 0 9 0 b 0 10 0 12 0 11 0 13 0 10 0 12 0 11 0 13 0 0 0 2 0 1 0 3 0 0 0 2 0 1 0 3
  //   0 20 0 22 0 21 0 23 0 20 0 22 0 21 0 23
endmodule
