// Logisim project UEROM_v2.circ as structural Verilog: 1 circuit, main circuit main
module main (
  input  DATA,
  input  IR0,
  input  IR1,
  input  IR2,
  input  IR3,
  input  RST
);

  wire and_1_out, and_2_out, and_3_out, and_4_out, and_5_out, and_6_out, CLK_out, not_1_out, not_2_out,
       not_3_out, not_4_out, not_5_out;
  wire [4:1] CAR_q;
  wire [7:0] rom_1_data;

  and and_1 (and_1_out, IR3, not_1_out, IR1, IR0);
  Clock CLK (.out(CLK_out));
  not not_1 (not_1_out, IR2);
  not not_2 (not_2_out, IR0);
  and and_2 (and_2_out, IR3, not_1_out, IR1, not_2_out);
  D_Flip_Flop IEN (.D(DATA), .clk(and_3_out), .Q(CAR_q[4]), .reset(RST));  // open: Qn, preset
  and and_3 (and_3_out, and_2_out, CLK_out);
  D_Flip_Flop OEN (.D(DATA), .clk(and_4_out), .Q(CAR_q[3]), .reset(RST));  // open: Qn, preset
  and and_4 (and_4_out, and_1_out, CLK_out);
  ROM #(.addrWidth(9)) rom_1 (.addr({IR3, IR2, IR1, IR0, CAR_q, DATA}), .data(rom_1_data));
  and and_5 (and_5_out, IR3, IR2, not_3_out, not_2_out);
  not not_3 (not_3_out, IR1);
  not not_4 (not_4_out, CLK_out);
  not not_5 (not_5_out, CLK_out);
  D_Flip_Flop CAR (.D(rom_1_data[6]), .clk(not_4_out), .Q(CAR_q[1]), .reset(RST));  // open: Qn, preset
  D_Flip_Flop RREG (.D(rom_1_data[7]), .clk(not_5_out), .Q(CAR_q[2]), .reset(RST));  // open: Qn, preset
  LED JMP (.in(and_5_out));
  LED FLF (.in(rom_1_data[0]));
  LED SKZ (.in(rom_1_data[1]));
  LED IOC (.in(rom_1_data[3]));
  LED FL0 (.in(rom_1_data[4]));
  LED DAT (.in(rom_1_data[5]));
  and and_6 (and_6_out, rom_1_data[2], CLK_out);
  LED WRT (.in(and_6_out));
  LED RR (.in(CAR_q[2]));

  // Notes on the sheet:
  //   contents of rom_1 (hex, n*v repeats v):
  //   32*10 0 0 40 40 0 0 40 40 0 0 40 40 0 0 40 40 0 80 40 c0 0 80 40 c0 0 80 40 c0 0 80 40 c0 0 80 80 40
  //   80 40 40 c0 0 80 80 40 80 40 40 c0 0 80 80 40 80 40 40 c0 0 80 80 40 80 40 40 c0 0 0 4*40 c0 c0 0 0
  //   4*40 c0 c0 0 0 40 80 40 80 c0 40 0 0 40 80 40 80 c0 40 34*80 c0 c0 80 80 c0 c0 80 80 c0 c0 80 80 c0
  //   c0 80 80 c0 c0 80 0 c0 40 80 80 c0 c0 80 0 c0 40 0 0 40 40 80 80 c0 c0 0 0 40 40 80 80 c0 c0 0 80 40
  //   c0 80 80 c0 c0 0 80 40 c0 80 80 c0 c0 0 0 40 40 80 80 c0 c0 0 0 40 40 80 80 c0 c0 0 80 40 c0 80 0 c0
  //   40 0 80 40 c0 80 0 c0 40 0 0 40 40 a0 a0 e0 e0 4 4 44 44 a4 a4 e4 e4 0 0 40 40 a0 a0 e0 e0 4 4 44 44
  //   a4 a4 e4 e4 20 20 60 60 80 80 c0 c0 24 24 64 64 84 84 c4 c4 20 20 60 60 80 80 c0 c0 24 24 64 64 84
  //   84 c4 c4 0 0 40 40 80 80 c0 c0 0 0 40 40 80 80 c0 c0 0 0 40 40 80 80 c0 c0 0 0 40 40 80 80 c0 c0 0 0
  //   40 40 80 80 c0 c0 0 0 40 40 80 80 c0 c0 0 0 40 40 80 80 c0 c0 0 0 40 40 80 80 c0 c0 0 0 40 40 80 80
  //   c0 c0 0 0 40 40 80 80 c0 c0 0 0 40 40 80 80 c0 c0 0 0 40 40 80 80 c0 c0 8 8 48 48 88 88 c8 c8 8 8 48
  //   48 88 88 c8 c8 8 8 48 48 88 88 c8 c8 8 8 48 48 88 88 c8 c8 2 2 42 42 82 82 c2 c2 2 2 42 42 82 82 c2
  //   c2 2 2 42 42 82 82 c2 c2 2 2 42 42 82 82 c2 c2 1 1 41 41 81 81 c1 c1 1 1 41 41 81 81 c1 c1 1 1 41 41
  //   81 81 c1 c1 1 1 41 41 81 81 c1 c1
endmodule
