// Logisim project UEROM_v3.circ as structural Verilog: 1 circuit, main circuit main
module main (
  input  DATA,
  input  IR0,
  input  IR1,
  input  IR2,
  input  IR3,
  input  RST
);

  wire and_1_out, and_2_out, and_3_out, and_4_out, and_5_out, and_6_out, and_7_out, and_8_out, and_9_out,
       CAR_qn, CLK_out, nand_1_out, not_1_out, not_2_out, not_3_out, not_5_out, not_6_out, not_7_out,
       not_8_out, or_5_out, or_6_out, RREG_qn, SKZREG_q;
  wire [7:0] rom_1_data;
  wire [8:1] CAR_q;

  Clock CLK (.out(CLK_out));
  or or_1 (CAR_q[5], SKZREG_q, IR0);
  not not_1 (not_1_out, CAR_q[5]);
  or or_2 (CAR_q[6], SKZREG_q, IR1);
  not not_2 (not_2_out, CAR_q[6]);
  or or_3 (CAR_q[7], SKZREG_q, IR2);
  not not_3 (not_3_out, CAR_q[7]);
  // NOT_Gate not_4 has open pins: in=CAR_q[8], out=open
  or or_4 (CAR_q[8], SKZREG_q, IR3);
  and and_1 (and_1_out, CAR_q[8], CAR_q[7], not_2_out, CAR_q[5]);
  and and_2 (and_2_out, CAR_q[8], not_3_out, CAR_q[6], CAR_q[5]);
  and and_3 (and_3_out, CAR_q[8], not_3_out, CAR_q[6], not_1_out);
  D_Flip_Flop IEN (.D(DATA), .clk(and_4_out), .Q(CAR_q[4]), .reset(RST));  // open: Qn, preset
  and and_4 (and_4_out, and_3_out, CLK_out);
  D_Flip_Flop OEN (.D(DATA), .clk(and_5_out), .Q(CAR_q[3]), .reset(RST));  // open: Qn, preset
  and and_5 (and_5_out, and_2_out, CLK_out);
  ROM #(.addrWidth(9)) rom_1 (.addr({CAR_q, DATA}), .data(rom_1_data));
  and and_6 (and_6_out, rom_1_data[1], DATA);
  or or_5 (or_5_out, and_6_out, and_1_out);
  not not_5 (not_5_out, nand_1_out);
  or or_6 (or_6_out, not_5_out, and_7_out);
  and and_7 (and_7_out, SKZREG_q, rom_1_data[0]);
  D_Flip_Flop CAR (.D(rom_1_data[6]), .clk(not_6_out), .Q(CAR_q[1]), .Qn(CAR_qn), .reset(RST));  // open: preset
  not not_6 (not_6_out, CLK_out);
  D_Flip_Flop RREG (.D(rom_1_data[7]), .clk(not_7_out), .Q(CAR_q[2]), .Qn(RREG_qn), .reset(RST));  // open: preset
  not not_7 (not_7_out, CLK_out);
  D_Flip_Flop SKZREG (.D(or_5_out), .clk(not_8_out), .Q(SKZREG_q), .reset(RST));  // open: Qn, preset
  not not_8 (not_8_out, CLK_out);
  nand nand_1 (nand_1_out, or_6_out, rom_1_data[0]);
  and and_8 (and_8_out, nand_1_out, rom_1_data[0]);
  LED FLF (.in(and_8_out));
  LED JMP (.in(rom_1_data[3]));
  LED FL0 (.in(rom_1_data[4]));
  LED DAT (.in(rom_1_data[5]));
  and and_9 (and_9_out, rom_1_data[2], CLK_out);
  LED WRT (.in(and_9_out));
  LED RTN (.in(and_1_out));
  LED C (.in(CAR_q[1]));
  LED QC (.in(CAR_qn));
  LED RR (.in(CAR_q[2]));
  LED QRR (.in(RREG_qn));

  // Notes on the sheet:
  //   contents of rom_1 (hex, n*v repeats v):
  //   32*10 0 0 40 40 0 0 40 40 0 0 40 40 0 0 40 40 0 80 40 c0 0 80 40 c0 0 80 40 c0 0 80 40 c0 0 80 80 40
  //   80 40 40 c0 0 80 80 40 80 40 40 c0 0 80 80 40 80 40 40 c0 0 80 80 40 80 40 40 c0 0 0 4*40 c0 c0 0 0
  //   4*40 c0 c0 0 0 40 80 40 80 c0 40 0 0 40 80 40 80 c0 40 34*80 c0 c0 80 80 c0 c0 80 80 c0 c0 80 80 c0
  //   c0 80 80 c0 c0 80 0 c0 40 80 80 c0 c0 80 0 c0 40 0 0 40 40 80 80 c0 c0 0 0 40 40 80 80 c0 c0 0 80 40
  //   c0 80 80 c0 c0 0 80 40 c0 80 80 c0 c0 0 0 40 40 80 80 c0 c0 0 0 40 40 80 80 c0 c0 0 80 40 c0 80 0 c0
  //   40 0 80 40 c0 80 0 c0 40 0 0 40 40 a0 a0 e0 e0 4 4 44 44 a4 a4 e4 e4 0 0 40 40 a0 a0 e0 e0 4 4 44 44
  //   a4 a4 e4 e4 20 20 60 60 80 80 c0 c0 24 24 64 64 84 84 c4 c4 20 20 60 60 80 80 c0 c0 24 24 64 64 84
  //   84 c4 c4 0 0 40 40 80 80 c0 c0 0 0 40 40 80 80 c0 c0 0 0 40 40 80 80 c0 c0 0 0 40 40 80 80 c0 c0 0 0
  //   40 40 80 80 c0 c0 0 0 40 40 80 80 c0 c0 0 0 40 40 80 80 c0 c0 0 0 40 40 80 80 c0 c0 8 8 48 48 88 88
  //   c8 c8 8 8 48 48 88 88 c8 c8 8 8 48 48 88 88 c8 c8 8 8 48 48 88 88 c8 c8 0 0 40 40 80 80 c0 c0 0 0 40
  //   40 80 80 c0 c0 0 0 40 40 80 80 c0 c0 0 0 40 40 80 80 c0 c0 2 2 42 42 82 82 c2 c2 2 2 42 42 82 82 c2
  //   c2 2 2 42 42 82 82 c2 c2 2 2 42 42 82 82 c2 c2 1 1 41 41 81 81 c1 c1 1 1 41 41 81 81 c1 c1 1 1 41 41
  //   81 81 c1 c1 1 1 41 41 81 81 c1 c1
endmodule
